# Fritzing sketch nixie_clock (saved by Fritzing 0.9.4)

parts:
  Arduino_Nano = Arduino Nano (Rev3.0)
  DS3231 = ZS-042 RTC Module
  LED_board = female pin header, 3 pins [form="♀ (female)"]
  R1 = Resistor [tolerance=±5% resistance=220 package=THT]
  DC_power_supply = Battery block 9V
  C1 = Ceramic Capacitor [capacitance="100 nF" package="0603 [SMD, multilayer]"]

nets:
  GND: Arduino_Nano.GND, DS3231.GND, LED_board.pin3, DC_power_supply.-, C1.0
  N1: Arduino_Nano.D7, R1.Pin_0
  N2: Arduino_Nano.VIN, DC_power_supply.+
  N3: Arduino_Nano.5V, LED_board.pin1, C1.1
  N4: Arduino_Nano.A5, DS3231.SCL
  N5: Arduino_Nano.A4, DS3231.SDA
  3V3: Arduino_Nano.3V3, DS3231.VCC
  N6: LED_board.pin2, R1.Pin_1

notes:
  DS3231
  Arduino Nano
  220 Ohm
  Vcc
  Din
  GND
  LED board
  DC power supply
  100 nF
